# Fritzing sketch Meteostanice (saved by Fritzing 0.8.7b)
breadboards: 1

parts:
  U2 = ESP32S-HiLetgo [part_number=ESP32S-HiLetgo]
  SW-1 = Vibration sensor module
  YL-83_-_Detection_Board1 = YL-83 Rain Sensor - Detection Board
  YL-83_-_Control_Board1 = YL-83 Rain Sensor - Control Board
  BMP280_Breakout1 = BMP280 Breakout Board [part_number=BMP280]
  Q1 = NPN-Transistor [package="TO92 [THT]"]
  Mod1 = CJMCU-811

nets:
  N1: U2.EN, SW-1.Digital_output
  N2: U2.GPIO34, YL-83_-_Control_Board1.DO
  GND: U2.GND, SW-1.Ground, YL-83_-_Control_Board1.GND, BMP280_Breakout1.GND, Mod1.GND
  VCC: U2.VIN, SW-1.vcc, YL-83_-_Control_Board1.VCC, Q1.E
  N3: U2.GPIO5, Q1.B
  N4: U2.GPIO21, BMP280_Breakout1.SDA, Mod1.SDA
  N5: U2.GPIO22, BMP280_Breakout1.SCL, Mod1.SCL
  N6: YL-83_-_Detection_Board1.POS, YL-83_-_Control_Board1.POS
  N7: YL-83_-_Detection_Board1.NEG, YL-83_-_Control_Board1.NEG
  VCC_2: BMP280_Breakout1.VCC, Q1.C, Mod1.VCC

notes:
  Senzor otřesu
  Senzor deště
  BMP280
  CJMCU-811

custom parts:
  ESP32S-HiLetgo: HiLetgo ESP-WROOM-32 ESP32 ESP-32S Development Board 2.4GHz Dual-Mode WiFi + Bluetooth Dual Cores Microcontroller The ESP32 integrated with Antenna switches, RF Balun, power amplifiers, low-noise amplifiers, filters, and management modules, and the entire solution occupies the least area of PCB. 2.4 GHz Wi-Fi plus Bluetooth dual-mode chip, with TSMC Ultra-low power consumption 40nm technology,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
  Vibration sensor module: Single-roller type full induction trigger switch. When no vibration or tilt, the product is ON conduction state, and in the steady state, when a vibration or tilt, the switch will be rendered instantly disconnect the conductive resistance increases, generating a current pulse signal, thereby triggering circuit. The default state of the swith is close Digital output Supply voltage:3.3V-5V On-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
  YL-83 Rain Sensor - Detection Board: The YL-83 is a rain sensor that has more resistance when dry and less resistance when wet. The module runs at 5V.
  YL-83 Rain Sensor - Control Board: The YL-83 is a rain sensor that has more resistance when dry and less resistance when wet. The module runs at 5V.
  BMP280 Breakout Board: This is a breakout board for the Bosch Sensortec BMP280, "an absolute barometric pressure sensor especially designed for mobile applications." The operation range is 300 to 1100 hPa. Supply voltage is 1.2 to 3.6V. Operating temperature range is -40 to +85 °C.
  CJMCU-811: The CCS811 is an ultra-low power digital gas sensor solution which integrates a metal oxide (MOX) gas sensor to detect a wide range of Volatile Organic Compounds (VOCs) for indoor air quality monitoring with a microcontroller unit (MCU), which includes an Analog-to-Digital converter (ADC), and an I²C interface.
